// Logisim project carryleftshifter.circ as structural Verilog: 1 circuit, main circuit main
module main (
  input  c0,
  input  e2,
  input  e1,
  input  e0,
  output s3,
  output s2,
  output s1,
  output s0
);

  wire and_1_out, and_2_out, and_3_out, and_4_out, not_1_out;

  not not_1 (not_1_out, c0);
  and and_1 (and_1_out, e2, c0);
  and and_2 (and_2_out, not_1_out, e1);
  and and_3 (and_3_out, c0, e1);
  and and_4 (and_4_out, not_1_out, e0);
  and and_5 (s3, not_1_out, e2);
  or or_1 (s2, and_1_out, and_2_out);
  or or_2 (s1, and_3_out, and_4_out);
  and and_6 (s0, c0, e0);

  // Notes on the sheet:
  //   Carry left shifter 3-4
endmodule
