// Logisim project codificador.circ as structural Verilog: 1 circuit, main circuit main
module main (
  input  e0,
  input  e1,
  input  e2,
  input  e3,
  input  s1,
  input  s0,
  output s0_2,
  output s1_2,
  output v,
  output s3,
  output s2,
  output s1_3,
  output s0_3
);

  wire and_5_out, and_6_out, and_7_out, not_1_out, not_2_out, not_3_out, not_4_out, not_5_out, not_6_out;

  ExactlyOne xor_1 (.out(v), .in0(e0), .in1(e1), .in3(e2), .in4(e3));
  not not_1 (not_1_out, s1);
  not not_2 (not_2_out, s0);
  not not_3 (not_3_out, e0);
  not not_4 (not_4_out, e1);
  not not_5 (not_5_out, e2);
  not not_6 (not_6_out, e3);
  and and_1 (s3, s1, s0);
  and and_2 (s2, s1, not_2_out);
  and and_3 (s1_3, s0, not_1_out);
  and and_4 (s0_3, not_2_out, not_1_out);
  and and_5 (and_5_out, not_3_out, not_5_out, not_6_out, e1);
  and and_6 (and_6_out, not_4_out, not_3_out, not_6_out, e2);
  and and_7 (and_7_out, not_5_out, not_3_out, not_4_out, e3);
  or or_1 (s0_2, and_5_out, and_7_out);
  or or_2 (s1_2, and_6_out, and_7_out);

  // Notes on the sheet:
  //   Codificador
  //   Decodificador
endmodule
