// Logisim project decodificador.circ as structural Verilog: 1 circuit, main circuit main
module main (
  input  s1,
  input  s0,
  output s3,
  output s2,
  output s1_2,
  output s0_2
);

  wire not_1_out, not_2_out;

  not not_1 (not_1_out, s1);
  not not_2 (not_2_out, s0);
  and and_1 (s3, s1, s0);
  and and_2 (s2, s1, not_2_out);
  and and_3 (s1_2, s0, not_1_out);
  and and_4 (s0_2, not_2_out, not_1_out);
endmodule
