// Logisim project extensor.circ as structural Verilog: 2 circuits, main circuit main
module main (
  input  in_1,
  input  in_2,
  input  in_3,
  input  in_4,
  input  load,
  input  ext,
  output out_7,
  output out_8,
  output out_9,
  output out_10
);

  wire clock_1_out;
  wire [3:0] multiplexer_1_out;

  Clock clock_1 (.out(clock_1_out));
  D_Flip_Flop #(.trigger("high")) d_ff_1 (
    .clk(clock_1_out), .D(multiplexer_1_out[3]), .Q(out_7));  // open: Qn, preset, en, reset
  D_Flip_Flop #(.trigger("high")) d_ff_2 (
    .clk(clock_1_out), .D(multiplexer_1_out[2]), .Q(out_8));  // open: Qn, preset, en, reset
  D_Flip_Flop #(.trigger("high")) d_ff_3 (
    .clk(clock_1_out), .D(multiplexer_1_out[1]), .Q(out_9));  // open: Qn, preset, en, reset
  D_Flip_Flop #(.trigger("high")) d_ff_4 (
    .clk(clock_1_out), .D(multiplexer_1_out[0]), .Q(out_10));  // open: Qn, preset, en, reset
  Multiplexer #(.select(2), .width(4)) multiplexer_1 (
    .in0({out_7, out_8, out_9, out_10}), .in1({{3{out_9}}, out_10}), .in2({in_1, in_2, in_3, in_4}),
    .in3({{3{in_3}}, in_4}), .out(multiplexer_1_out), .sel({load, ext}), .en(1'b1));

  // Notes on the sheet:
  //   MUX output
  //   Qext
  //   Q
  //   Iext
  //   I
endmodule

module Registro (
  input  in_1,
  input  in_2,
  output out_3
);

  wire and_1_out, and_2_out, clock_1_out, d_ff_1_q, not_1_out;

  Clock clock_1 (.out(clock_1_out));
  D_Flip_Flop #(.trigger("high")) d_ff_1 (.clk(clock_1_out), .D(out_3), .Q(d_ff_1_q));  // open: Qn, preset, en, reset
  not not_1 (not_1_out, in_2);
  and and_1 (and_1_out, d_ff_1_q, not_1_out);
  and and_2 (and_2_out, in_1, in_2);
  or or_1 (out_3, and_1_out, and_2_out);
endmodule
