// Logisim project practica2.circ as structural Verilog: 1 circuit, main circuit main
module main (
  input  A,
  input  B,
  input  c0,
  input  c1,
  input  A_2,
  input  e0,
  input  A_3,
  input  B_2,
  input  C,
  input  A_4,
  input  B_3,
  input  C_2,
  output out_13,
  output out_14,
  output out_15,
  output out_16,
  output out_17,
  output out_18,
  output out_19,
  output out_20
);

  wire and_1_out, and_2_out, nand_1_out, nor_1_out, not_1_out, not_2_out, not_3_out, not_4_out, not_5_out,
       not_6_out, not_7_out;

  nand nand_1 (nand_1_out, A, B);
  not not_1 (not_1_out, A_3);
  not not_2 (not_2_out, B_2);
  not not_3 (not_3_out, B_3);
  nand nand_2 (out_15, A_2, A_2);
  nor nor_1 (nor_1_out, not_1_out, not_2_out);
  and and_1 (and_1_out, A_4, not_3_out);
  and and_2 (and_2_out, B_3, C_2);
  nand nand_3 (out_13, nand_1_out, nand_1_out);
  not not_4 (not_4_out, nor_1_out);
  not not_5 (not_5_out, C);
  nor nor_2 (out_18, not_4_out, not_5_out);
  or or_1 (out_20, and_1_out, and_2_out);
  not not_6 (not_6_out, c0);
  not not_7 (not_7_out, c1);
  and and_3 (out_14, not_7_out, e0, not_6_out);
  and and_4 (out_16, c0, e0, not_7_out);
  and and_5 (out_17, not_6_out, e0, c1);
  and and_6 (out_19, c0, e0, c1);

  // Notes on the sheet:
  //   Ej. 4
  //   Ej. 5
  //   Ej. 6
  //   Circuito AND
  //   Circuito NOT
  //   f(A,B,C) = A·B·C
  //   f(A,B,C) = A·!B+B·C
  //   Ej. 7
  //   Demultiplexor
endmodule
