// Logisim project registrosalidarestringida.circ as structural Verilog: 2 circuits, main circuit main
module main (
  input  read,
  input  in_2,
  input  in_3,
  input  in_4,
  input  in_5,
  input  load,
  output out_7,
  output out_8,
  output out_9,
  output out_10
);

  wire clock_1_out;
  wire [3:0] d_ff_4_q, multiplexer_1_out;

  Clock clock_1 (.out(clock_1_out));
  assign out_7 = read ? d_ff_4_q[3] : 1'bz;  // Controlled_Buffer controlled_buffer_1
  D_Flip_Flop #(.trigger("high")) d_ff_1 (
    .clk(clock_1_out), .D(multiplexer_1_out[3]), .Q(d_ff_4_q[3]));  // open: Qn, preset, en, reset
  assign out_8 = read ? d_ff_4_q[2] : 1'bz;  // Controlled_Buffer controlled_buffer_2
  D_Flip_Flop #(.trigger("high")) d_ff_2 (
    .clk(clock_1_out), .D(multiplexer_1_out[2]), .Q(d_ff_4_q[2]));  // open: Qn, preset, en, reset
  assign out_9 = read ? d_ff_4_q[1] : 1'bz;  // Controlled_Buffer controlled_buffer_3
  D_Flip_Flop #(.trigger("high")) d_ff_3 (
    .clk(clock_1_out), .D(multiplexer_1_out[1]), .Q(d_ff_4_q[1]));  // open: Qn, preset, en, reset
  D_Flip_Flop #(.trigger("high")) d_ff_4 (
    .clk(clock_1_out), .D(multiplexer_1_out[0]), .Q(d_ff_4_q[0]));  // open: Qn, preset, en, reset
  assign out_10 = read ? d_ff_4_q[0] : 1'bz;  // Controlled_Buffer controlled_buffer_4
  Multiplexer #(.width(4)) multiplexer_1 (
    .in0(d_ff_4_q), .in1({in_2, in_3, in_4, in_5}), .out(multiplexer_1_out), .sel(load), .en(1'b1));

  // Notes on the sheet:
  //   Q
  //   I
endmodule

module Registro (
  input  in_1,
  input  in_2,
  output out_3
);

  wire and_1_out, and_2_out, clock_1_out, d_ff_1_q, not_1_out;

  Clock clock_1 (.out(clock_1_out));
  not not_1 (not_1_out, in_2);
  D_Flip_Flop #(.trigger("high")) d_ff_1 (.clk(clock_1_out), .D(out_3), .Q(d_ff_1_q));  // open: Qn, preset, en, reset
  and and_1 (and_1_out, d_ff_1_q, not_1_out);
  and and_2 (and_2_out, in_1, in_2);
  or or_1 (out_3, and_1_out, and_2_out);
endmodule
