// Logisim project sumador.circ as structural Verilog: 1 circuit, main circuit main
module main (
  input  A0,
  input  B0,
  input  A1,
  input  B1,
  input  A2,
  input  B2,
  input  A3,
  input  B3,
  output _2_0,
  output _2_1,
  output _2_2,
  output _2_3,
  output CARRY,
  output OVERFLOW,
  output NEGATIVE,
  output ZERO
);

  wire and_1_out, and_2_out, and_3_out, and_4_out, and_5_out, and_6_out, and_7_out, nor_1_out, nor_2_out,
       or_1_out, or_2_out, xor_1_out, xor_2_out, xor_3_out;

  and and_1 (and_1_out, B1, A1);
  and and_2 (and_2_out, B2, A2);
  and and_3 (and_3_out, B3, A3);
  and and_4 (and_4_out, A0, B0);
  xor xor_1 (xor_1_out, A1, B1);
  or or_1 (or_1_out, and_1_out, and_5_out);
  xor xor_2 (xor_2_out, A2, B2);
  or or_2 (or_2_out, and_2_out, and_6_out);
  xor xor_3 (xor_3_out, A3, B3);
  or or_3 (CARRY, and_3_out, and_7_out);
  and and_5 (and_5_out, and_4_out, xor_1_out);
  and and_6 (and_6_out, or_1_out, xor_2_out);
  and and_7 (and_7_out, or_2_out, xor_3_out);
  xor xor_4 (OVERFLOW, CARRY, or_2_out);
  xor xor_5 (_2_0, A0, B0);
  xor xor_6 (_2_1, and_4_out, xor_1_out);
  xor xor_7 (_2_2, or_1_out, xor_2_out);
  xor xor_8 (_2_3, or_2_out, xor_3_out);
  nor nor_1 (nor_1_out, _2_0, _2_1);
  and and_8 (ZERO, nor_1_out, nor_2_out);
  nor nor_2 (nor_2_out, _2_2, _2_3);

  assign NEGATIVE = _2_3;

  // Notes on the sheet:
  //   Sumador de 4 bits
  //   C
endmodule
