// Logisim project sumador2.circ as structural Verilog: 1 circuit, main circuit main
module main (
  input  Cin,
  input  A,
  input  B,
  output suma,
  output Cout
);

  wire and_1_out, and_2_out, and_3_out, and_4_out, and_5_out, and_6_out, and_7_out, not_1_out, not_2_out,
       not_3_out, or_1_out, or_2_out;

  not not_1 (not_1_out, A);
  not not_2 (not_2_out, B);
  and and_1 (and_1_out, A, not_2_out);
  and and_2 (and_2_out, not_1_out, B);
  and and_3 (and_3_out, not_1_out, not_2_out);
  and and_4 (and_4_out, A, B);
  or or_1 (or_1_out, and_1_out, and_2_out);
  or or_2 (or_2_out, and_3_out, and_4_out);
  not not_3 (not_3_out, Cin);
  and and_5 (and_5_out, not_3_out, or_1_out);
  and and_6 (and_6_out, Cin, or_1_out);
  and and_7 (and_7_out, Cin, or_2_out);
  or or_3 (suma, and_5_out, and_7_out);
  or or_4 (Cout, and_6_out, and_4_out);

  // Notes on the sheet:
  //   A·!B
  //   !A·B
  //   !A·!B
  //   A·B
  //   !A·B + A·!B
  //   A·B + !A·!B
endmodule
